# Fritzing sketch Raspberry-Pi-design (saved by Fritzing 0.9.3b)
breadboards: 1

parts:
  Raspberry_Pi_1 = Raspberry Pi 3 [part_number=RPI-3-V1.2]
  U2 = mystery part, 6 pins [chip_label="iAQ air quality sensor"]
  U3 = mystery part, 7 pins [chip_label=GPS]
  LED1 = LED - 5mm [color="Red (633nm)" package="5 mm [THT]"]
  R1 = Resistor [tolerance=±5% resistance=220 package=THT]
  R2 = Resistor [tolerance=±5% resistance=220 package=THT]
  R3 = Resistor [tolerance=±5% resistance=220 package=THT]

nets:
  N1: Raspberry_Pi_1.3v3, U2.pin6, U3.pin1, R2.Pin_0, R3.Pin_1
  N2: Raspberry_Pi_1.GPIO2, U2.pin4, R2.Pin_1
  N3: Raspberry_Pi_1.GPIO3, U2.pin2, R3.Pin_0
  N4: Raspberry_Pi_1.GIPO24, LED1.cathode
  N5: Raspberry_Pi_1.GIPO15, U3.pin5
  N6: Raspberry_Pi_1.GIPO14, U3.pin6
  N7: U2.pin3, U3.pin2, R1.Pin_1
  N8: LED1.anode, R1.Pin_0
