# Fritzing sketch Raspberry Pi design (saved by Fritzing 0.9.3b)
breadboards: 1

parts:
  Raspberry_Pi_1 = Raspberry Pi 3 [part_number=RPI-3-V1.2]
  R1 = Resistor [tolerance=±5% resistance=220 package=THT]
  U2 = mystery part, 6 pins [chip_label="iAQ air quality sensor"]
  U3 = mystery part, 7 pins [chip_label=GPS]
  U4 = mystery part, 7 pins [chip_label=GPS]  # not connected
  U5 = mystery part, 6 pins [chip_label="iAQ air quality sensor"]  # not connected

nets:
  N1: Raspberry_Pi_1.3v3, R1.Pin_0
  N2: Raspberry_Pi_1.GPIO2, U2.pin4
  N3: Raspberry_Pi_1.GPIO3, U2.pin2
  N4: Raspberry_Pi_1.GIPO18, U3.pin7
  N5: Raspberry_Pi_1.GIPO15, U3.pin3
  N6: Raspberry_Pi_1.GIPO14, U3.pin2
  N7: Raspberry_Pi_1.GND, U2.pin3, U3.pin5
  N8: R1.Pin_1, U2.pin6, U3.pin6

notes:
  Raspberry Pi 3 has built in WiFi for uploading data collected from GPS and Air quality module
